# Fritzing sketch edison_schematics (saved by Fritzing 0.9.3b)
circuit board: 8.46667cm x 5.64444cm
breadboards: 1

parts:
  Part1 = Intel Edison Arduinobreakout
  S1 = Pushbutton [package="[THT]"]
  R1 = Resistor [tolerance=±5% resistance=1k package="0402 [SMD]"]
  R2 = Resistor [tolerance=±5% resistance=220 package="0402 [SMD]"]
  LED1 = smd LED [color="Red (633nm)" package="1206 [SMD]"]

nets (from the breadboard view):
  N1: Part1.D12/MISO, R1.Pin_0
  N2: Part1.D13/SCK, R2.Pin_0
  N3: Part1.GND, S1.Pin_1, S1.Pin_2, LED1.cathode
  N4: S1.Pin_3, S1.Pin_4, R1.Pin_1
  N5: R2.Pin_1, LED1.anode
